// Logisim project Comparadorbeta.circ as structural Verilog: 1 circuit, main circuit main
module main (
  input  in_1,
  input  in_2,
  input  in_3,
  input  in_4,
  input  in_5,
  input  in_6,
  output E,
  output F,
  output G,
  output A,
  output C,
  output D
);

  wire and_1_out, and_2_out, and_3_out, and_4_out, and_5_out, and_6_out, and_7_out, and_8_out, and_9_out,
       C_out, not_1_out, xnor_1_out, xnor_2_out, xnor_3_out, xor_1_out, xor_2_out, xor_3_out;

  xnor xnor_1 (xnor_1_out, in_1, in_4);
  xnor xnor_2 (xnor_2_out, in_2, in_5);
  xnor xnor_3 (xnor_3_out, in_3, in_6);
  xor xor_1 (xor_1_out, in_3, 1'b1);
  xor xor_2 (xor_2_out, in_2, 1'b1);
  xor xor_3 (xor_3_out, in_1, 1'b1);
  and and_1 (and_1_out, in_6, xor_1_out);
  and and_2 (and_2_out, in_5, xor_2_out);
  and and_3 (and_3_out, in_4, xor_3_out);
  and and_4 (and_4_out, and_1_out, 1'b1);
  and and_5 (and_5_out, and_2_out, 1'b1);
  and and_6 (and_6_out, and_3_out, 1'b1);
  and and_7 (and_7_out, 1'b1, and_4_out);
  or u_C (C_out, and_7_out, and_5_out);
  or C_2 (A, C_out, and_6_out);
  and and_8 (and_8_out, xnor_1_out, xnor_2_out, xnor_3_out);
  not not_1 (not_1_out, A);
  and and_9 (and_9_out, and_8_out, not_1_out);
  xor xor_4 (C, and_8_out, not_1_out);
  or or_1 (D, C, and_9_out);
  or or_2 (F, C, A);
  or or_3 (E, A, C, and_9_out);
  or or_4 (G, A, C, and_9_out);
endmodule
