// Logisim project Decenas definitivo zelda.circ as structural Verilog: 1 circuit, main circuit main
module main (
  input  A,
  input  B,
  input  C,
  input  D,
  input  E,
  output a2,
  output b2,
  output c2,
  output d2,
  output e2,
  output g2
);

  wire and_1_out, and_2_out, and_3_out, and_4_out, and_5_out, and_6_out, and_7_out, not_1_out, not_2_out,
       not_3_out, not_4_out, not_5_out, not_6_out, not_7_out, not_8_out, not_9_out, not_10_out, or_1_out,
       or_2_out, or_3_out, or_4_out, or_5_out, or_6_out;

  not not_1 (not_1_out, A);
  or or_1 (or_1_out, B, C);
  or or_2 (or_2_out, D, A, C);
  not not_2 (not_2_out, E);
  not not_3 (not_3_out, D);
  and and_1 (and_1_out, B, C, D);
  not not_4 (not_4_out, A);
  and and_2 (and_2_out, not_4_out, B, D);
  not not_5 (not_5_out, A);
  and and_3 (and_3_out, not_5_out, B, C);
  not not_6 (not_6_out, B);
  not not_7 (not_7_out, C);
  or or_3 (or_3_out, B, C);
  and and_4 (and_4_out, A, not_8_out, C);
  not not_8 (not_8_out, B);
  and and_5 (and_5_out, A, B, not_9_out);
  not not_9 (not_9_out, C);
  not not_10 (not_10_out, D);
  or or_4 (or_4_out, B, C);
  or or_5 (or_5_out, B, E, not_2_out);
  or or_6 (or_6_out, A, D, not_3_out, not_1_out);
  and and_6 (and_6_out, A, not_6_out, not_7_out);
  and and_7 (and_7_out, A, B, C, not_10_out);
  and and_8 (b2, or_2_out, or_5_out, or_6_out);
  or or_7 (e2, and_4_out, and_5_out, and_7_out);
  and and_9 (a2, A, or_1_out);
  or or_8 (c2, and_1_out, and_2_out, and_3_out, and_6_out);
  and and_10 (d2, A, or_3_out);
  and and_11 (g2, A, or_4_out);
endmodule
