// Logisim project MULTIPLICADOR2ORI.circ as structural Verilog: 1 circuit, main circuit main
module main (
  input  A3,
  input  A2,
  input  in_3,
  input  A0,
  input  B0,
  input  B1,
  input  B2,
  input  B3,
  output out_9,
  output out_10,
  output out_11,
  output out_12,
  output out_13,
  output out_14,
  output out_15,
  output out_16
);

  wire and_1_out, and_2_out, and_3_out, and_4_out, and_5_out, and_6_out, and_7_out, and_8_out, and_9_out,
       and_10_out, and_11_out, and_12_out, and_13_out, and_14_out, and_15_out, main_2_out_4, main_2_out_5,
       main_3_out_5, main_4_out_4, main_4_out_5, main_5_out_4, main_5_out_5, main_6_out_5, main_7_out_4,
       main_7_out_5, main_8_out_4, main_8_out_5, main_9_out_5, main_10_out_4, main_10_out_5, main_11_out_5,
       main_12_out_5;

  and and_1 (and_1_out, A3, B3);
  sumadores_main main_1 (.in_1(main_3_out_5), .in_2(main_2_out_5), .in_3(and_1_out), .out_5(out_9), .out_4(out_10));
  and and_2 (and_2_out, A3, B2);
  sumadores_main main_2 (
    .in_1(main_5_out_5), .in_2(main_4_out_5), .in_3(and_2_out), .out_5(main_2_out_5), .out_4(main_2_out_4));
  and and_3 (and_3_out, A2, B3);
  sumadores_main main_3 (
    .in_1(main_6_out_5), .in_2(main_2_out_4), .in_3(and_3_out), .out_5(main_3_out_5), .out_4(out_11));
  and and_4 (and_4_out, A3, B1);
  sumadores_main main_4 (
    .in_1(main_7_out_5), .in_2(and_4_out), .in_3(1'b0), .out_5(main_4_out_5), .out_4(main_4_out_4));
  and and_5 (and_5_out, A2, B2);
  sumadores_main main_5 (
    .in_1(main_8_out_5), .in_2(main_4_out_4), .in_3(and_5_out), .out_5(main_5_out_5), .out_4(main_5_out_4));
  and and_6 (and_6_out, in_3, B3);
  sumadores_main main_6 (
    .in_1(main_9_out_5), .in_2(main_5_out_4), .in_3(and_6_out), .out_5(main_6_out_5), .out_4(out_12));
  and and_7 (and_7_out, A3, B0);
  and and_8 (and_8_out, A2, B1);
  sumadores_main main_7 (
    .in_1(main_10_out_5), .in_2(and_7_out), .in_3(and_8_out), .out_5(main_7_out_5), .out_4(main_7_out_4));
  and and_9 (and_9_out, in_3, B2);
  sumadores_main main_8 (
    .in_1(main_11_out_5), .in_2(main_7_out_4), .in_3(and_9_out), .out_5(main_8_out_5), .out_4(main_8_out_4));
  and and_10 (and_10_out, A0, B3);
  sumadores_main main_9 (.in_1(1'b0), .in_2(main_8_out_4), .in_3(and_10_out), .out_5(main_9_out_5), .out_4(out_13));
  and and_11 (and_11_out, A2, B0);
  and and_12 (and_12_out, in_3, B1);
  sumadores_main main_10 (
    .in_1(main_12_out_5), .in_2(and_11_out), .in_3(and_12_out), .out_5(main_10_out_5), .out_4(main_10_out_4));
  and and_13 (and_13_out, A0, B2);
  sumadores_main main_11 (.in_1(1'b0), .in_2(main_10_out_4), .in_3(and_13_out), .out_5(main_11_out_5), .out_4(out_14));
  and and_14 (and_14_out, in_3, B0);
  and and_15 (and_15_out, A0, B1);
  sumadores_main main_12 (.in_1(1'b0), .in_2(and_14_out), .in_3(and_15_out), .out_5(main_12_out_5), .out_4(out_16));
  and and_16 (out_15, A0, B0);
endmodule
