// Logisim project Memoria.circ as structural Verilog: 1 circuit, main circuit main
module main (
);

  wire button_1_out, undriven, undriven_2, undriven_3, undriven_4, undriven_5;
  wire [7:0] register_1_q, register_2_q, register_3_q, register_4_q, register_5_q, register_6_q;

  Button button_1 (.out(button_1_out));
  Register register_1 (.Q(register_1_q), .clk(button_1_out), .clr(undriven));  // open: D, en
  Register register_2 (.D(register_1_q), .en(undriven), .Q(register_2_q), .clk(button_1_out), .clr(undriven_2));
  Register register_3 (.D(register_2_q), .en(undriven_2), .Q(register_3_q), .clk(button_1_out), .clr(undriven_3));
  Register register_4 (.D(register_5_q), .en(undriven_4), .Q(register_4_q), .clk(button_1_out), .clr(undriven_5));
  Register register_5 (.D(register_3_q), .en(undriven_3), .Q(register_5_q), .clk(button_1_out), .clr(undriven_4));
  Register register_6 (.D(register_4_q), .en(undriven_5), .Q(register_6_q), .clk(button_1_out));  // open: clr
  LED led_1 (.in(register_6_q[0]));
  // Pins of 1 and 8 bits meet at register_6_q
endmodule
