// Logisim project PROYECTO.circ as structural Verilog: 2 circuits, main circuit Dec
module main (
  input  [3:0] in_1,
  input  in_2,
  input  [3:0] in_3,
  input  [2:0] in_4
);

  wire a1_1_a_2, a1_1_b_2, a1_1_c_2, a1_1_d_2, a1_1_e, a1_1_f_2, a1_1_g, and_1_out, and_2_out, button_1_out,
       main_1_a_2, main_1_b_2, main_1_c_2, main_1_d_2, main_1_e, main_1_f, main_1_g, main_2_out_9,
       main_2_out_10, main_2_out_11, main_2_out_12, main_2_out_13, main_2_out_14, main_2_out_15,
       main_2_out_16, main_3_a_2, main_3_b_2, main_3_c_2, main_3_d_2, main_3_e, main_3_f, main_3_g, main_4_a,
       main_4_c, main_4_d, main_4_e, main_4_f, main_4_g, main_5_out_10, main_5_out_11, main_5_out_12,
       main_5_out_13, main_5_out_14, main_5_out_15, main_6_out_3, main_6_out_4, main_7_p6, main_7_p7,
       main_7_p8, main_7_p9, main_7_p10, main_7_p11;

  display_multiplicador_main main_1 (
    .A(main_2_out_9), .B(main_2_out_10), .C(main_2_out_11), .D(main_2_out_12), .a_2(main_1_a_2),
    .b_2(main_1_b_2), .c_2(main_1_c_2), .d_2(main_1_d_2), .e(main_1_e), .f(main_1_f), .g(main_1_g));
  MULTIPLICADOR2ORI_main main_2 (
    .A3(in_3[3]), .A2(in_3[2]), .in_3(in_3[1]), .A0(in_3[0]), .out_9(main_2_out_9), .out_10(main_2_out_10),
    .out_11(main_2_out_11), .out_12(main_2_out_12), .out_13(main_2_out_13), .out_14(main_2_out_14),
    .out_16(main_2_out_16), .out_15(main_2_out_15), .B0(in_1[0]), .B1(in_1[1]), .B2(in_1[2]), .B3(in_1[3]));
  display_multiplicador_main main_3 (
    .A(main_2_out_13), .B(main_2_out_14), .C(main_2_out_16), .D(main_2_out_15), .a_2(main_3_a_2),
    .b_2(main_3_b_2), .c_2(main_3_c_2), .d_2(main_3_d_2), .e(main_3_e), .f(main_3_f), .g(main_3_g));
  Comparadorbeta_main main_4 (
    .A(main_4_a), .C(main_4_c), .D(main_4_d), .E(main_4_e), .F(main_4_f), .G(main_4_g), .in_3(in_4[0]),
    .in_1(in_4[2]), .in_2(in_4[1]), .in_4(in_1[3]), .in_5(in_1[2]), .in_6(in_1[1]));
  _7_Segment_Display u_7_segment_display_1 (
    .g(main_1_g), .f(main_1_f), .a(main_1_a_2), .b(main_1_b_2), .e(main_1_e), .d(main_1_d_2), .c(main_1_c_2));  // open: dp
  and and_1 (and_1_out, main_4_c, main_4_d, main_4_e, main_4_f, main_4_g);
  _7_Segment_Display u_7_segment_display_2 (
    .g(main_3_g), .f(main_3_f), .a(main_3_a_2), .b(main_3_b_2), .e(main_3_e), .d(main_3_d_2), .c(main_3_c_2));  // open: dp
  LED led_1 (.in(and_1_out));
  SM3_main main_5 (
    .out_14(main_5_out_14), .C(in_2), .out_15(main_5_out_15), .out_10(main_5_out_10), .out_11(main_5_out_11),
    .out_12(main_5_out_12), .out_13(main_5_out_13), .a_2(in_1[2]), .a_4(in_1[0]), .a_3(in_1[1]), .b(in_3[3]),
    .in_6(in_3[2]), .in_7(in_3[1]), .in_8(in_3[0]), .a(in_1[3]));
  _7_Segment_Display u_7_segment_display_3 (
    .g(main_4_g), .f(main_4_f), .a(main_4_a), .e(main_4_e), .d(main_4_d), .c(main_4_c));  // open: b, dp
  LED led_2 (.in(main_2_out_15));
  LED led_3 (.in(main_2_out_16));
  LED led_4 (.in(main_2_out_14));
  LED led_5 (.in(main_2_out_13));
  LED led_6 (.in(main_2_out_12));
  LED led_7 (.in(main_2_out_11));
  LED led_8 (.in(main_2_out_10));
  LED led_9 (.in(main_2_out_9));
  and and_2 (and_2_out, main_4_a, main_4_f, main_4_g, main_4_e);
  Button button_1 (.out(button_1_out));
  Reloj_main main_6 (.in_1(and_2_out), .in_2(button_1_out), .out_3(main_6_out_3), .out_4(main_6_out_4));
  // Decenitas_main main_7: pin names not known; wires that end beside it: main_5_out_15, main_5_out_10, main_5_out_11, main_5_out_12, main_5_out_13, main_7_p6, main_7_p7, main_7_p8, main_7_p9, main_7_p10, main_7_p11
  a1 a1_1 (
    .a_2(a1_1_a_2), .A(main_5_out_15), .B(main_5_out_10), .C(main_5_out_11), .D(main_5_out_12),
    .F(main_5_out_13), .b_2(a1_1_b_2), .c_2(a1_1_c_2), .d_2(a1_1_d_2), .e(a1_1_e), .g(a1_1_g), .f_2(a1_1_f_2));
  _7_Segment_Display u_7_segment_display_4 (.g(main_5_out_14));  // open: f, a, b, e, d, c, dp
  LED led_10 (.in(main_6_out_3));
  LED led_11 (.in(main_6_out_4));
  _7_Segment_Display u_7_segment_display_5 (
    .g(main_7_p11), .a(main_7_p6), .b(main_7_p7), .e(main_7_p10), .d(main_7_p9), .c(main_7_p8));  // open: f, dp
  _7_Segment_Display u_7_segment_display_6 (
    .g(a1_1_g), .f(a1_1_f_2), .a(a1_1_a_2), .b(a1_1_b_2), .e(a1_1_e), .d(a1_1_d_2), .c(a1_1_c_2));  // open: dp
endmodule

module Dec (
  input  A,
  input  B,
  input  C,
  input  D,
  input  E,
  output a2,
  output b2,
  output c2,
  output d2,
  output e2,
  output g2
);

  wire and_1_out, and_2_out, and_3_out, and_4_out, and_5_out, and_6_out, and_7_out, not_1_out, not_2_out,
       not_3_out, not_4_out, not_5_out, not_6_out, not_7_out, or_1_out, or_2_out, or_3_out, or_4_out,
       or_5_out;

  or or_1 (or_1_out, B, C);
  or or_2 (or_2_out, A, B);
  or or_3 (or_3_out, A, C, D);
  and and_1 (and_1_out, B, C, D);
  not not_1 (not_1_out, A);
  and and_2 (and_2_out, not_1_out, B, D);
  not not_2 (not_2_out, A);
  and and_3 (and_3_out, not_2_out, B, C);
  not not_3 (not_3_out, B);
  not not_4 (not_4_out, C);
  or or_4 (or_4_out, B, C);
  and and_4 (and_4_out, A, not_5_out, C);
  not not_5 (not_5_out, B);
  and and_5 (and_5_out, A, B, not_6_out);
  not not_6 (not_6_out, C);
  not not_7 (not_7_out, D);
  or or_5 (or_5_out, B, C);
  and and_6 (and_6_out, A, not_3_out, not_4_out);
  and and_7 (and_7_out, A, B, C, not_7_out);
  or or_6 (e2, and_4_out, and_5_out, and_7_out);
  and and_8 (a2, A, or_1_out);
  and and_9 (b2, or_2_out, or_3_out);
  or or_7 (c2, and_1_out, and_2_out, and_3_out, and_6_out);
  and and_10 (d2, A, or_4_out);
  and and_11 (g2, A, or_5_out);
endmodule
