// Logisim project Reloj.circ as structural Verilog: 1 circuit, main circuit main
module main (
  input  in_1,
  input  in_2,
  output out_3,
  output out_4
);

  wire clock_1_out, d_ff_1_q, d_ff_2_q, d_ff_3_q, d_ff_3_qn, d_ff_4_q, d_ff_5_qn, not_1_out;

  D_Flip_Flop d_ff_1 (.clk(in_1), .D(d_ff_3_qn), .Q(d_ff_1_q), .reset(in_2));  // open: Qn, preset, en
  not not_1 (not_1_out, d_ff_3_q);
  D_Flip_Flop d_ff_2 (.clk(in_1), .D(d_ff_1_q), .Q(d_ff_2_q), .reset(in_2));  // open: Qn, preset, en
  Clock clock_1 (.out(clock_1_out));
  D_Flip_Flop d_ff_3 (.clk(in_1), .D(d_ff_2_q), .Q(d_ff_3_q), .Qn(d_ff_3_qn), .reset(in_2));  // open: preset, en
  D_Flip_Flop d_ff_4 (.clk(clock_1_out), .D(d_ff_5_qn), .Q(d_ff_4_q), .preset(not_1_out));  // open: Qn, en, reset
  D_Flip_Flop d_ff_5 (
    .clk(clock_1_out), .D(d_ff_4_q), .Q(out_3), .Qn(d_ff_5_qn), .reset(not_1_out));  // open: preset, en
  and and_1 (out_4, d_ff_5_qn, d_ff_3_q);
endmodule
