// Logisim project SM3.circ as structural Verilog: 1 circuit, main circuit main
module main (
  input  a,
  input  a_2,
  input  a_3,
  input  a_4,
  input  b,
  input  in_6,
  input  in_7,
  input  in_8,
  input  C,
  output out_10,
  output out_11,
  output out_12,
  output out_13,
  output out_14,
  output out_15
);

  wire and_1_out, and_2_out, and_3_out, and_4_out, and_5_out, and_6_out, and_7_out, and_8_out, and_9_out,
       and_10_out, and_11_out, and_12_out, and_13_out, and_14_out, and_15_out, and_16_out, and_17_out,
       C_2_out, C_3_out, C_4_out, C_5_out, C_7_out, C_out, xor_2_out, xor_3_out, xor_4_out, xor_6_out,
       xor_7_out, xor_8_out, xor_9_out, xor_10_out, xor_11_out, xor_12_out, xor_13_out, xor_14_out,
       xor_15_out, xor_16_out, xor_17_out, xor_18_out, xor_19_out, xor_20_out, xor_21_out, xor_22_out;

  // XOR_Gate xor_1 is placed but not wired
  xor xor_2 (xor_2_out, a, out_14);
  xor xor_3 (xor_3_out, a_2, out_14);
  xor xor_4 (xor_4_out, xor_2_out, xor_7_out);
  and and_1 (and_1_out, xor_2_out, xor_7_out);
  and and_2 (and_2_out, xor_4_out, C_2_out);
  or u_C (C_out, and_1_out, and_2_out);
  xor xor_5 (out_15, C, C_out);
  xor xor_6 (xor_6_out, a_3, out_14);
  xor xor_7 (xor_7_out, C, xor_15_out);
  xor S (out_10, xor_4_out, C_2_out);
  xor xor_8 (xor_8_out, a_4, C);
  xor xor_9 (xor_9_out, a_3, C);
  xor xor_10 (xor_10_out, a_2, C);
  xor xor_11 (xor_11_out, a, C);
  xor xor_12 (xor_12_out, a_4, out_14);
  and and_3 (and_3_out, xor_3_out, xor_13_out);
  and and_4 (and_4_out, xor_14_out, C_3_out);
  or C_2 (C_2_out, and_3_out, and_4_out);
  and and_5 (and_5_out, in_8, xor_8_out);
  and and_6 (and_6_out, in_7, xor_9_out);
  and and_7 (and_7_out, in_6, xor_10_out);
  and and_8 (and_8_out, b, xor_11_out);
  xor xor_13 (xor_13_out, C, xor_18_out);
  xor xor_14 (xor_14_out, xor_3_out, xor_13_out);
  xor S_2 (out_11, xor_14_out, C_3_out);
  and and_9 (and_9_out, xor_6_out, xor_16_out);
  or C_3 (C_3_out, and_9_out, and_15_out);
  and and_10 (and_10_out, C, and_11_out);
  and and_11 (and_11_out, and_5_out, C);
  or C_4 (C_4_out, and_10_out, and_12_out);
  and and_12 (and_12_out, and_6_out, C);
  or C_5 (C_5_out, C_4_out, and_13_out);
  and and_13 (and_13_out, and_7_out, C);
  or C_6 (out_14, C_5_out, and_14_out);
  and and_14 (and_14_out, and_8_out, C);
  xor xor_15 (xor_15_out, b, out_14);
  xor xor_16 (xor_16_out, C, xor_20_out);
  xor xor_17 (xor_17_out, xor_6_out, xor_16_out);
  and and_15 (and_15_out, xor_17_out, C_7_out);
  xor S_3 (out_12, xor_17_out, C_7_out);
  xor xor_18 (xor_18_out, in_6, out_14);
  and and_16 (and_16_out, xor_12_out, xor_21_out);
  or C_7 (C_7_out, and_16_out, and_17_out);
  xor xor_19 (xor_19_out, in_8, out_14);
  xor xor_20 (xor_20_out, in_7, out_14);
  xor xor_21 (xor_21_out, C, xor_19_out);
  xor xor_22 (xor_22_out, xor_12_out, xor_21_out);
  and and_17 (and_17_out, xor_22_out, C);
  xor S_4 (out_13, xor_22_out, C);
endmodule
