// Logisim project Unidades5.circ as structural Verilog: 1 circuit, main circuit a1
module a1 (
  input  A,
  input  B,
  input  C,
  input  D,
  input  F,
  output a_2,
  output b_2,
  output d_2,
  output c_2,
  output e,
  output out_11,
  output g
);

  wire and_1_out, and_2_out, and_3_out, and_4_out, and_5_out, not_1_out, not_2_out, not_3_out, not_4_out,
       not_5_out, not_6_out, not_7_out, not_8_out, not_9_out, not_10_out, not_11_out, not_12_out, not_13_out,
       not_14_out, not_15_out, not_16_out, not_17_out, not_18_out, not_19_out, not_20_out, not_21_out,
       not_22_out, not_23_out, not_24_out, not_25_out, not_26_out, not_27_out, not_28_out, not_29_out,
       not_30_out, not_31_out, not_32_out, not_33_out, not_34_out, not_35_out, not_36_out, not_37_out,
       not_38_out, not_39_out, not_40_out, not_41_out, not_42_out, not_43_out, not_44_out, not_45_out,
       not_46_out, not_47_out, not_48_out, not_49_out, not_50_out, not_51_out, not_52_out, not_53_out,
       not_54_out, not_55_out, not_56_out, not_57_out, not_58_out, not_59_out, not_60_out, not_61_out,
       not_62_out, not_63_out, not_64_out, not_65_out, not_66_out, not_67_out, not_68_out, not_69_out,
       not_70_out, not_71_out, not_72_out, not_73_out, not_74_out, not_75_out, not_76_out, not_77_out,
       not_78_out, not_79_out, not_80_out, not_81_out, not_82_out, not_83_out, not_84_out, not_85_out,
       not_86_out, not_87_out, not_88_out, not_89_out, not_90_out, not_91_out, not_92_out, not_93_out,
       not_94_out, not_95_out, not_96_out, not_97_out, not_98_out, not_99_out, not_100_out, not_101_out,
       not_102_out, not_103_out, not_104_out, not_105_out, not_106_out, not_107_out, or_1_out, or_2_out,
       or_3_out, or_4_out, or_5_out, or_6_out, or_7_out, or_8_out, or_9_out, or_10_out, or_11_out, or_12_out,
       or_13_out, or_14_out, or_15_out, or_16_out, or_17_out, or_18_out, or_19_out, or_20_out, or_21_out,
       or_22_out, or_23_out, or_24_out, or_25_out, or_26_out, or_27_out, or_28_out, or_29_out, or_30_out,
       or_31_out, or_32_out, or_33_out, or_34_out, or_35_out, or_36_out, or_37_out, or_38_out, or_39_out,
       or_40_out, or_41_out;

  not not_1 (not_1_out, C);
  not not_2 (not_2_out, F);
  not not_3 (not_3_out, F);
  not not_4 (not_4_out, B);
  not not_5 (not_5_out, F);
  not not_6 (not_6_out, B);
  not not_7 (not_7_out, B);
  not not_8 (not_8_out, C);
  not not_9 (not_9_out, D);
  not not_10 (not_10_out, D);
  not not_11 (not_11_out, C);
  not not_12 (not_12_out, F);
  not not_13 (not_13_out, A);
  not not_14 (not_14_out, F);
  not not_15 (not_15_out, C);
  not not_16 (not_16_out, F);
  not not_17 (not_17_out, D);
  not not_18 (not_18_out, A);
  not not_19 (not_19_out, C);
  not not_20 (not_20_out, D);
  not not_21 (not_21_out, A);
  not not_22 (not_22_out, B);
  not not_23 (not_23_out, D);
  not not_24 (not_24_out, F);
  not not_25 (not_25_out, B);
  not not_26 (not_26_out, D);
  not not_27 (not_27_out, C);
  not not_28 (not_28_out, D);
  not not_29 (not_29_out, F);
  not not_30 (not_30_out, A);
  not not_31 (not_31_out, F);
  not not_32 (not_32_out, F);
  not not_33 (not_33_out, C);
  not not_34 (not_34_out, B);
  not not_35 (not_35_out, D);
  not not_36 (not_36_out, B);
  not not_37 (not_37_out, D);
  not not_38 (not_38_out, A);
  not not_39 (not_39_out, C);
  not not_40 (not_40_out, F);
  not not_41 (not_41_out, A);
  not not_42 (not_42_out, B);
  not not_43 (not_43_out, C);
  not not_44 (not_44_out, D);
  not not_45 (not_45_out, A);
  not not_46 (not_46_out, C);
  not not_47 (not_47_out, C);
  not not_48 (not_48_out, D);
  not not_49 (not_49_out, C);
  not not_50 (not_50_out, D);
  not not_51 (not_51_out, A);
  not not_52 (not_52_out, A);
  not not_53 (not_53_out, B);
  not not_54 (not_54_out, F);
  not not_55 (not_55_out, A);
  not not_56 (not_56_out, D);
  not not_57 (not_57_out, F);
  not not_58 (not_58_out, C);
  not not_59 (not_59_out, D);
  not not_60 (not_60_out, D);
  not not_61 (not_61_out, B);
  not not_62 (not_62_out, A);
  not not_63 (not_63_out, C);
  not not_64 (not_64_out, F);
  not not_65 (not_65_out, B);
  not not_66 (not_66_out, F);
  not not_67 (not_67_out, C);
  not not_68 (not_68_out, C);
  not not_69 (not_69_out, F);
  not not_70 (not_70_out, B);
  not not_71 (not_71_out, D);
  not not_72 (not_72_out, A);
  not not_73 (not_73_out, F);
  not not_74 (not_74_out, A);
  not not_75 (not_75_out, B);
  not not_76 (not_76_out, C);
  not not_77 (not_77_out, F);
  not not_78 (not_78_out, A);
  not not_79 (not_79_out, D);
  not not_80 (not_80_out, B);
  not not_81 (not_81_out, F);
  not not_82 (not_82_out, A);
  not not_83 (not_83_out, C);
  not not_84 (not_84_out, F);
  not not_85 (not_85_out, A);
  not not_86 (not_86_out, D);
  not not_87 (not_87_out, C);
  not not_88 (not_88_out, F);
  not not_89 (not_89_out, B);
  not not_90 (not_90_out, D);
  not not_91 (not_91_out, F);
  not not_92 (not_92_out, B);
  not not_93 (not_93_out, D);
  not not_94 (not_94_out, F);
  not not_95 (not_95_out, A);
  not not_96 (not_96_out, F);
  or or_1 (or_1_out, not_18_out, B, not_19_out, not_20_out);
  not not_97 (not_97_out, A);
  not not_98 (not_98_out, C);
  not not_99 (not_99_out, A);
  not not_100 (not_100_out, B);
  not not_101 (not_101_out, D);
  not not_102 (not_102_out, F);
  not not_103 (not_103_out, A);
  not not_104 (not_104_out, B);
  not not_105 (not_105_out, C);
  not not_106 (not_106_out, D);
  or or_2 (or_2_out, A, B, C, D, not_32_out);
  or or_3 (or_3_out, A, B, not_33_out, D, F);
  or or_4 (or_4_out, A, not_34_out, not_1_out, not_35_out, F);
  or or_5 (or_5_out, A, not_36_out, C, not_37_out, not_2_out);
  or or_6 (or_6_out, not_38_out, B, not_39_out, D, not_40_out);
  or or_7 (or_7_out, not_41_out, not_42_out, not_43_out, not_44_out, not_3_out);
  or or_8 (or_8_out, not_45_out, not_4_out, C, D, F);
  or or_9 (or_9_out, A, B, not_46_out, D, not_5_out);
  or or_10 (or_10_out, A, B, not_47_out, not_48_out, F);
  or or_11 (or_11_out, A, B, not_49_out, not_50_out, F);
  or or_12 (or_12_out, not_51_out, B, C, D, F);
  or or_13 (or_13_out, not_52_out, not_53_out, C, D, not_54_out);
  or or_14 (or_14_out, not_55_out, not_6_out, C, not_56_out, F);
  or or_15 (or_15_out, A, not_7_out, not_57_out, not_58_out, not_59_out);
  or or_16 (or_16_out, A, B, C, not_60_out, F);
  or or_17 (or_17_out, A, not_61_out, not_8_out, D, F);
  or or_18 (or_18_out, not_62_out, B, not_63_out, not_9_out, F);
  or or_19 (or_19_out, A, C, D, not_64_out);
  or or_20 (or_20_out, A, not_65_out, C, not_66_out);
  or or_21 (or_21_out, A, B, not_67_out, D, F);
  or or_22 (or_22_out, A, B, not_68_out, not_10_out, not_69_out);
  or or_23 (or_23_out, A, not_70_out, not_11_out, not_71_out, F);
  or or_24 (or_24_out, not_72_out, B, D, not_73_out);
  or or_25 (or_25_out, not_74_out, not_75_out, not_76_out, not_77_out);
  or or_26 (or_26_out, not_78_out, C, not_79_out, not_12_out);
  not not_107 (not_107_out, B);
  and and_1 (and_1_out, not_80_out, D, not_81_out);
  and and_2 (and_2_out, not_82_out, not_83_out, not_84_out);
  and and_3 (and_3_out, not_85_out, B, not_86_out, not_14_out);
  and and_4 (and_4_out, A, B, C, D);
  and and_5 (and_5_out, not_87_out, D, not_88_out);
  or or_27 (or_27_out, A, not_89_out, not_15_out, D);
  or or_28 (or_28_out, A, B, C, not_16_out);
  or or_29 (or_29_out, A, B, C, not_17_out);
  or or_30 (or_30_out, A, B, not_90_out, not_91_out);
  or or_31 (or_31_out, A, not_92_out, C, not_93_out, not_94_out);
  or or_32 (or_32_out, not_95_out, B, D, not_96_out);
  or or_33 (or_33_out, not_21_out, not_22_out, not_23_out, not_24_out);
  or or_34 (or_34_out, A, B, C, D);
  or or_35 (or_35_out, A, not_25_out, C, not_26_out);
  or or_36 (or_36_out, A, B, not_27_out, not_28_out, not_29_out);
  or or_37 (or_37_out, not_30_out, B, D, not_31_out);
  or or_38 (or_38_out, not_97_out, B, not_98_out, D);
  or or_39 (or_39_out, not_99_out, not_100_out, not_101_out, not_102_out);
  or or_40 (or_40_out, not_103_out, not_104_out, not_105_out, not_106_out, F);
  or or_41 (or_41_out, C, D, not_107_out, F, not_13_out);
  or or_42 (e, and_1_out, and_2_out, and_3_out, and_4_out, and_5_out);
  and and_6 (g, or_34_out, or_35_out, or_36_out, or_37_out, or_38_out, or_39_out, or_40_out);
  and and_7 (out_11, or_27_out, or_28_out, or_29_out, or_30_out, or_31_out, or_32_out, or_1_out, or_33_out);
  and and_8 (a_2, or_2_out, or_3_out, or_4_out, or_5_out, or_6_out, or_7_out, or_8_out);
  and and_9 (b_2, or_9_out, or_10_out, or_11_out, or_15_out, or_12_out, or_13_out, or_14_out);
  and and_10 (c_2, or_16_out, or_17_out, or_18_out);
  and and_11 (d_2, or_19_out, or_20_out, or_21_out, or_22_out, or_41_out, or_23_out, or_24_out, or_25_out, or_26_out);
endmodule
