// Logisim project correcion f sumador (1).circ as structural Verilog: 1 circuit, main circuit main
module main (
  input  A,
  input  B,
  input  C,
  input  D,
  input  E
);

  wire and_1_out, not_1_out, not_2_out, not_3_out, not_4_out, not_5_out, not_6_out, not_7_out, not_8_out,
       not_9_out, not_10_out, not_11_out, not_12_out, not_13_out, not_14_out, not_15_out, not_16_out,
       not_17_out, not_18_out, or_1_out, or_2_out, or_3_out, or_4_out, or_5_out, or_6_out, or_7_out, or_8_out;

  not not_1 (not_1_out, B);
  not not_2 (not_2_out, C);
  not not_3 (not_3_out, E);
  not not_4 (not_4_out, D);
  not not_5 (not_5_out, D);
  not not_6 (not_6_out, E);
  not not_7 (not_7_out, B);
  not not_8 (not_8_out, D);
  not not_9 (not_9_out, E);
  not not_10 (not_10_out, A);
  not not_11 (not_11_out, E);
  not not_12 (not_12_out, A);
  not not_13 (not_13_out, C);
  not not_14 (not_14_out, D);
  not not_15 (not_15_out, A);
  not not_16 (not_16_out, B);
  not not_17 (not_17_out, D);
  not not_18 (not_18_out, E);
  or or_1 (or_1_out, A, not_1_out, not_2_out, D);
  or or_2 (or_2_out, A, B, C, not_3_out);
  or or_3 (or_3_out, A, B, C, not_4_out);
  or or_4 (or_4_out, A, B, not_5_out, not_6_out);
  or or_5 (or_5_out, A, not_7_out, C, not_8_out, not_9_out);
  or or_6 (or_6_out, not_10_out, B, D, not_11_out);
  or or_7 (or_7_out, not_12_out, B, not_13_out, not_14_out);
  or or_8 (or_8_out, not_15_out, not_16_out, not_17_out, not_18_out);
  and and_1 (and_1_out, or_1_out, or_2_out, or_3_out, or_4_out, or_5_out, or_6_out, or_7_out, or_8_out);
  LED f (.in(and_1_out));
endmodule
