// Logisim project display multiplicador.circ as structural Verilog: 1 circuit, main circuit main
module main (
  input  A,
  input  B,
  input  C,
  input  D,
  output a_2,
  output b_2,
  output c_2,
  output d_2,
  output e,
  output f,
  output g
);

  wire not_1_out, not_2_out, not_3_out, not_4_out, not_5_out, not_6_out, not_7_out, not_8_out, not_9_out,
       not_10_out, not_11_out, not_12_out, not_13_out, not_14_out, not_15_out, not_16_out, not_17_out,
       not_18_out, not_19_out, not_20_out, not_21_out, not_22_out, not_23_out, not_24_out, not_25_out,
       not_26_out, not_27_out, not_28_out, not_29_out, not_30_out, not_31_out, not_32_out, not_33_out,
       not_34_out, not_35_out, not_36_out, not_37_out, not_38_out, not_39_out, not_40_out, not_41_out,
       not_42_out, not_43_out, not_44_out, not_45_out, not_46_out, or_1_out, or_2_out, or_3_out, or_4_out,
       or_5_out, or_6_out, or_7_out, or_8_out, or_9_out, or_10_out, or_11_out, or_12_out, or_13_out,
       or_14_out, or_15_out, or_16_out, or_17_out, or_18_out, or_19_out, or_20_out, or_21_out, or_22_out,
       or_23_out, or_24_out, or_25_out;

  not not_1 (not_1_out, D);
  not not_2 (not_2_out, A);
  not not_3 (not_3_out, B);
  not not_4 (not_4_out, D);
  not not_5 (not_5_out, C);
  not not_6 (not_6_out, D);
  not not_7 (not_7_out, D);
  not not_8 (not_8_out, B);
  not not_9 (not_9_out, A);
  not not_10 (not_10_out, B);
  not not_11 (not_11_out, D);
  not not_12 (not_12_out, C);
  not not_13 (not_13_out, B);
  not not_14 (not_14_out, C);
  not not_15 (not_15_out, D);
  not not_16 (not_16_out, B);
  not not_17 (not_17_out, A);
  not not_18 (not_18_out, C);
  not not_19 (not_19_out, D);
  not not_20 (not_20_out, B);
  not not_21 (not_21_out, D);
  not not_22 (not_22_out, A);
  not not_23 (not_23_out, B);
  not not_24 (not_24_out, A);
  not not_25 (not_25_out, C);
  not not_26 (not_26_out, D);
  not not_27 (not_27_out, B);
  not not_28 (not_28_out, C);
  not not_29 (not_29_out, A);
  not not_30 (not_30_out, B);
  not not_31 (not_31_out, A);
  not not_32 (not_32_out, B);
  not not_33 (not_33_out, C);
  not not_34 (not_34_out, B);
  or or_1 (or_1_out, B, C, not_6_out);
  not not_35 (not_35_out, B);
  not not_36 (not_36_out, C);
  or or_2 (or_2_out, not_35_out, not_36_out, not_37_out);
  not not_37 (not_37_out, D);
  not not_38 (not_38_out, A);
  not not_39 (not_39_out, C);
  or or_3 (or_3_out, A, not_7_out);
  or or_4 (or_4_out, A, not_8_out, C);
  not not_40 (not_40_out, A);
  not not_41 (not_41_out, D);
  or or_5 (or_5_out, not_9_out, not_10_out, C, not_11_out);
  not not_42 (not_42_out, D);
  or or_6 (or_6_out, A, not_43_out, not_44_out);
  not not_43 (not_43_out, C);
  not not_44 (not_44_out, D);
  or or_7 (or_7_out, A, B, not_12_out);
  or or_8 (or_8_out, A, B, C);
  or or_9 (or_9_out, A, not_13_out, not_14_out, not_15_out);
  not not_45 (not_45_out, A);
  not not_46 (not_46_out, B);
  or or_10 (or_10_out, A, B, C, not_1_out);
  or or_11 (or_11_out, A, not_16_out, C, D);
  or or_12 (or_12_out, not_2_out, not_3_out, C, not_4_out);
  or or_13 (or_13_out, not_17_out, B, not_18_out, not_19_out);
  or or_14 (or_14_out, A, not_20_out, C, not_21_out);
  or or_15 (or_15_out, not_22_out, not_23_out, D);
  or or_16 (or_16_out, not_24_out, not_25_out, not_26_out);
  or or_17 (or_17_out, not_27_out, not_28_out, D);
  or or_18 (or_18_out, not_29_out, not_30_out, D);
  or or_19 (or_19_out, not_31_out, not_32_out, not_33_out);
  or or_20 (or_20_out, A, not_34_out, C, D);
  or or_21 (or_21_out, not_38_out, B, not_39_out, D);
  or or_22 (or_22_out, not_40_out, B, C, not_41_out);
  or or_23 (or_23_out, A, B, not_42_out);
  or or_24 (or_24_out, not_45_out, not_46_out, C, D);
  or or_25 (or_25_out, A, B, not_5_out, D);
  and and_1 (d_2, or_20_out, or_1_out, or_2_out, or_21_out);
  and and_2 (e, or_3_out, or_4_out, or_22_out);
  and and_3 (g, or_8_out, or_9_out, or_24_out);
  and and_4 (a_2, or_10_out, or_11_out, or_12_out, or_13_out);
  and and_5 (b_2, or_14_out, or_15_out, or_16_out, or_17_out);
  and and_6 (f, or_5_out, or_23_out, or_6_out, or_7_out);
  and and_7 (c_2, or_25_out, or_18_out, or_19_out);
endmodule
